# Fritzing sketch Untitled Sketch arduino montage (saved by Fritzing 0.9.3b)
breadboards: 2

parts:
  Composant1 = Arduino Uno (Rev3)
  Thermi = Temperature Sensor (Thermistor) [thermistor_type=PTC package=THT]
  R4 = Resistor [tolerance=±5% resistance=10k package="0603 [SMD]"]
  DHT22 = Humidity and Temperature Sensor RHT03
  R5 = Resistor [tolerance=±5% resistance=220 package="0603 [SMD]"]
  MOSFET = Basic FET N-Channel [package="D2Pak [SMD]"]
  PC = Battery block 9V
  Res_Mos = Resistor [tolerance=±5% resistance=10k package=THT]
  J1 = Peltier Element
  part = Resistor [tolerance=±5% resistance=5.6k package=THT]
  Sonde = Temperature Sensor (Thermistor) [thermistor_type=NTC package=THT]

nets:
  N1: Composant1.A0, Thermi.pin_0, R4.Pin_1
  N2: Composant1.A1, part.Pin_1, Sonde.pin_1
  N3: Composant1.GND, Thermi.pin_1, DHT22.GND_2, MOSFET.source, PC.-
  N4: Composant1.D2, DHT22.Data-signal, R5.Pin_0
  N5: Composant1.D5_PWM, MOSFET.Gate, Res_Mos.Pin_1
  5V: Composant1.5V, R4.Pin_0, DHT22.Vcc, R5.Pin_1, PC.+, J1.pin2, part.Pin_0, Sonde.pin_0
  N6: MOSFET.drain, J1.pin1
